// Logisim project Mircoprocessor.circ as structural Verilog: 3 circuits, main circuit 8-bit  7 seg display
module _8_bit__7_seg_display (
  input  [7:0] in_1,
  output [3:0] out_2,
  output [3:0] out_3,
  output [3:0] out_4
);

  wire dabble_1_out_5, dabble_1_out_6, dabble_1_out_7, dabble_1_out_8, dabble_2_out_5, dabble_2_out_6,
       dabble_2_out_7, dabble_2_out_8, dabble_3_out_5, dabble_3_out_6, dabble_3_out_7, dabble_3_out_8,
       dabble_5_out_5, dabble_5_out_6, dabble_5_out_7, dabble_5_out_8, dabble_7_out_5, dabble_7_out_6,
       dabble_7_out_7;

  Dabble dabble_1 (
    .in_1(in_1[5]), .in_2(in_1[6]), .in_3(in_1[7]), .in_4(1'b0), .out_5(dabble_1_out_5),
    .out_6(dabble_1_out_6), .out_7(dabble_1_out_7), .out_8(dabble_1_out_8));
  Dabble dabble_2 (
    .in_1(in_1[3]), .in_2(dabble_3_out_5), .in_3(dabble_3_out_6), .in_4(dabble_3_out_7),
    .out_5(dabble_2_out_5), .out_6(dabble_2_out_6), .out_7(dabble_2_out_7), .out_8(dabble_2_out_8));
  Dabble dabble_3 (
    .in_1(in_1[4]), .in_2(dabble_1_out_5), .in_3(dabble_1_out_6), .in_4(dabble_1_out_7),
    .out_5(dabble_3_out_5), .out_6(dabble_3_out_6), .out_7(dabble_3_out_7), .out_8(dabble_3_out_8));
  Dabble dabble_4 (
    .in_1(in_1[1]), .in_2(dabble_5_out_5), .in_3(dabble_5_out_6), .in_4(dabble_5_out_7), .out_5(out_4[1]),
    .out_6(out_4[2]), .out_7(out_4[3]), .out_8(out_3[0]));
  Dabble dabble_5 (
    .in_1(in_1[2]), .in_2(dabble_2_out_5), .in_3(dabble_2_out_6), .in_4(dabble_2_out_7),
    .out_5(dabble_5_out_5), .out_6(dabble_5_out_6), .out_7(dabble_5_out_7), .out_8(dabble_5_out_8));
  Dabble dabble_6 (
    .in_1(dabble_5_out_8), .in_2(dabble_7_out_5), .in_3(dabble_7_out_6), .in_4(dabble_7_out_7),
    .out_5(out_3[1]), .out_6(out_3[2]), .out_7(out_3[3]), .out_8(out_2[0]));
  Dabble dabble_7 (
    .in_1(dabble_2_out_8), .in_2(dabble_3_out_8), .in_3(dabble_1_out_8), .in_4(1'b0), .out_5(dabble_7_out_5),
    .out_6(dabble_7_out_6), .out_7(dabble_7_out_7), .out_8(out_2[1]));

  assign out_2[3:2] = 2'b00;
  assign out_4[0] = in_1[0];
endmodule

module Dabble (
  input  in_1,
  input  in_2,
  input  in_3,
  input  in_4,
  output out_5,
  output out_6,
  output out_7,
  output out_8
);

  wire comparator_1_gt;
  wire [3:0] adder_1_out;

  Adder #(.width(4)) adder_1 (.a({in_4, in_3, in_2, in_1}), .b(4'b0011), .out(adder_1_out));  // open: cin, cout
  Comparator #(.width(4), .mode("unsigned")) comparator_1 (
    .a({in_4, in_3, in_2, in_1}), .b(4'b0100), .gt(comparator_1_gt));  // open: eq, lt
  Multiplexer #(.width(4), .disabled(0)) multiplexer_1 (
    .in0({in_4, in_3, in_2, in_1}), .in1(adder_1_out), .out({out_8, out_7, out_6, out_5}),
    .sel(comparator_1_gt));  // open: en
endmodule

module _8_bit_Microprocessor (
  input  [7:0] in_1,
  output [7:0] out_2
);

  wire clock_1_out, main_1_p5, main_1_p6, main_1_p7, main_1_p8, main_1_p9, main_1_p10, main_1_p11, main_2_p2;
  wire [2:0] main_1_p2;
  wire [3:0] n8_bit_7_seg_display_1_out_2, n8_bit_7_seg_display_1_out_3, n8_bit_7_seg_display_1_out_4,
       n8_bit_7_seg_display_2_out_2, n8_bit_7_seg_display_2_out_3, n8_bit_7_seg_display_2_out_4,
       n8_bit_7_seg_display_3_out_2, n8_bit_7_seg_display_3_out_3, n8_bit_7_seg_display_3_out_4,
       n8_bit_7_seg_display_4_out_2, n8_bit_7_seg_display_4_out_3, n8_bit_7_seg_display_4_out_4;
  wire [7:0] main_2_p1, register_1_p12, register_1_p13, register_1_p14;

  // controlunitprobably_main main_1: pin names not known; wires that end beside it: in_1, main_1_p2[0], main_1_p2[1], main_1_p2[2], main_1_p5, main_1_p6, main_1_p7, main_1_p8, main_1_p9, main_1_p10, main_1_p11
  // projectAUL__1__main main_2: pin names not known; wires that end beside it: main_2_p1, main_2_p2, main_1_p2, out_2
  Clock clock_1 (.out(clock_1_out));
  // Register register_1: pin names not known; wires that end beside it: out_2, main_1_p5, main_1_p6, main_1_p7, main_1_p8, main_1_p10, main_1_p11, 1'b1, main_1_p9, clock_1_out, main_2_p1, register_1_p12, register_1_p13, register_1_p14, main_2_p2
  _8_bit__7_seg_display u_8_bit_7_seg_display_1 (
    .in_1(main_2_p1), .out_2(n8_bit_7_seg_display_1_out_2), .out_3(n8_bit_7_seg_display_1_out_3),
    .out_4(n8_bit_7_seg_display_1_out_4));
  _8_bit__7_seg_display u_8_bit_7_seg_display_2 (
    .in_1(register_1_p14), .out_2(n8_bit_7_seg_display_2_out_2), .out_3(n8_bit_7_seg_display_2_out_3),
    .out_4(n8_bit_7_seg_display_2_out_4));
  _8_bit__7_seg_display u_8_bit_7_seg_display_3 (
    .in_1(register_1_p12), .out_2(n8_bit_7_seg_display_3_out_2), .out_3(n8_bit_7_seg_display_3_out_3),
    .out_4(n8_bit_7_seg_display_3_out_4));
  _8_bit__7_seg_display u_8_bit_7_seg_display_4 (
    .in_1(register_1_p13), .out_2(n8_bit_7_seg_display_4_out_2), .out_3(n8_bit_7_seg_display_4_out_3),
    .out_4(n8_bit_7_seg_display_4_out_4));
  Hex_Digit_Display hex_digit_display_1 (.value(n8_bit_7_seg_display_1_out_2));  // open: dp
  Hex_Digit_Display hex_digit_display_2 (.value(n8_bit_7_seg_display_3_out_2));  // open: dp
  Hex_Digit_Display hex_digit_display_3 (.value(n8_bit_7_seg_display_4_out_2));  // open: dp
  Hex_Digit_Display hex_digit_display_4 (.value(n8_bit_7_seg_display_2_out_2));  // open: dp
  Hex_Digit_Display hex_digit_display_5 (.value(n8_bit_7_seg_display_1_out_3));  // open: dp
  Hex_Digit_Display hex_digit_display_6 (.value(n8_bit_7_seg_display_1_out_4));  // open: dp
  Hex_Digit_Display hex_digit_display_7 (.value(n8_bit_7_seg_display_3_out_3));  // open: dp
  Hex_Digit_Display hex_digit_display_8 (.value(n8_bit_7_seg_display_3_out_4));  // open: dp
  Hex_Digit_Display hex_digit_display_9 (.value(n8_bit_7_seg_display_4_out_3));  // open: dp
  Hex_Digit_Display hex_digit_display_10 (.value(n8_bit_7_seg_display_4_out_4));  // open: dp
  Hex_Digit_Display hex_digit_display_11 (.value(n8_bit_7_seg_display_2_out_3));  // open: dp
  Hex_Digit_Display hex_digit_display_12 (.value(n8_bit_7_seg_display_2_out_4));  // open: dp
endmodule
